# Fritzing sketch FourButtonATTiny85I2C (saved by Fritzing 0.9.4)
stripboards: 3

parts:
  AT1 = ATTiny85 [chip_label=ATt85 package="DIP (Dual Inline) [THT]"]
  S0 = Pushbutton [package=THT]  # not connected
  S1 = Pushbutton [package=THT]
  S3 = Pushbutton [package=THT]
  S2 = Pushbutton [package=THT]  # not connected
  J1 = male pin header, 4 pins [form="♂ (male)"]
  J2 = male pin header, 4 pins [form="♂ (male)"]
  C1 = Ceramic Capacitor [capacitance=100nF package="100 mil [THT, multilayer]"]

nets:
  N1: AT1.PB3, S3.leg1
  N2: AT1.PB4, S1.leg1
  N3: AT1.GND, S1.leg0, S3.leg0, J1.pin2, J2.pin2, C1.1
  N4: AT1.PB0, J1.pin3, J2.pin3
  N5: AT1.PB2, J1.pin4, J2.pin4
  N6: AT1.VCC, J1.pin1, J2.pin1, C1.0

custom parts:
  ATTiny85: ATtiny85: Atmel 8-bit AVR Microcontroller with 2/4/8K Bytes In-System Programmable Flash
